// Logisim project MB.circ as structural Verilog
module main (
  input  A0,
  input  A1,
  input  A2,
  input  A4,
  input  B0,
  input  B1,
  input  B2,
  input  B3,
  input  \Soma_Subtração 
);

  wire ad_sub_dmx_1_overflow, ad_sub_dmx_1_s0, ad_sub_dmx_1_s1, ad_sub_dmx_1_s2, ad_sub_dmx_1_s3,
       display_1_a2, display_1_b2, display_1_c2, display_1_d2, display_1_e2, display_1_f, display_1_g,
       display_1_h;

  ad_sub_dmx ad_sub_dmx_1 (
    .A0(A0), .A1(A1), .A2(A2), .A3(A4), .B0(B0), .B1(B1), .B2(B2), .B3(B3), .AdSub(\Soma_Subtração ),
    .S0(ad_sub_dmx_1_s0), .S1(ad_sub_dmx_1_s1), .S2(ad_sub_dmx_1_s2), .S3(ad_sub_dmx_1_s3),
    .Overflow(ad_sub_dmx_1_overflow));
  Display display_1 (
    .a(ad_sub_dmx_1_s3), .b(ad_sub_dmx_1_s2), .c(ad_sub_dmx_1_s1), .d(ad_sub_dmx_1_s0),
    .e(ad_sub_dmx_1_overflow), .a2(display_1_a2), .b2(display_1_b2), .c2(display_1_c2), .d2(display_1_d2),
    .e2(display_1_e2), .f(display_1_f), .g(display_1_g), .h(display_1_h));
  _7_Segment_Display u_7_segment_display_1 (
    .g(display_1_g), .f(display_1_f), .a(display_1_a2), .b(display_1_b2), .e(display_1_e2), .d(display_1_d2),
    .c(display_1_c2), .dp(display_1_h));
endmodule

module somador (
  input  A3,
  input  A2,
  input  A1,
  input  A0,
  input  B3,
  input  B2,
  input  B1,
  input  B0,
  output S0,
  output S1,
  output S2,
  output S3,
  output S4
);

  wire and_1_out, and_2_out, and_3_out, and_4_out, and_5_out, and_6_out, and_7_out, and_8_out, and_9_out,
       and_10_out, and_11_out, and_12_out, and_13_out, and_14_out, and_15_out, and_16_out, and_17_out,
       and_18_out, and_19_out, and_20_out, and_21_out, and_22_out, and_23_out, and_24_out, and_25_out,
       and_26_out, and_27_out, and_28_out, and_29_out, and_30_out, and_31_out, and_32_out, and_33_out,
       and_34_out, and_35_out, and_36_out, and_37_out, and_38_out, and_39_out, and_40_out, and_41_out,
       and_42_out, and_43_out, and_44_out, and_45_out, and_46_out, and_47_out, and_48_out, and_49_out,
       and_50_out, and_51_out, and_52_out, and_53_out, and_54_out, and_55_out, and_56_out, and_57_out,
       and_58_out, and_59_out, and_60_out, and_61_out, and_62_out, and_63_out, and_64_out, and_65_out,
       and_66_out, and_67_out, and_68_out, and_69_out, and_70_out, and_71_out, and_72_out, and_73_out,
       and_74_out, and_75_out, not_1_out, not_2_out, not_3_out, not_4_out, not_5_out, not_6_out, not_7_out,
       not_8_out, not_9_out, not_10_out, not_11_out, not_12_out, not_13_out, not_14_out, not_15_out,
       not_16_out, not_17_out, not_18_out, not_19_out, not_20_out, not_21_out, not_22_out, not_23_out,
       not_24_out, not_25_out, not_26_out, not_27_out, not_28_out, not_29_out, not_30_out, not_31_out,
       not_32_out, not_33_out, not_34_out, not_35_out, not_36_out, not_37_out, not_38_out, not_39_out,
       not_40_out, not_41_out, not_42_out, not_43_out, not_44_out, not_45_out, not_46_out, not_47_out,
       not_48_out, not_49_out, not_50_out, not_51_out, not_52_out, not_53_out, not_54_out, not_55_out,
       not_56_out, not_57_out, not_58_out, not_59_out, not_60_out, not_61_out, not_62_out, not_63_out,
       not_64_out, not_65_out, not_66_out, not_67_out, not_68_out, not_69_out, not_70_out, not_71_out,
       not_72_out, not_73_out, not_74_out, not_75_out, not_76_out, not_77_out, not_78_out, not_79_out,
       not_80_out, not_81_out, not_82_out, not_83_out, not_84_out, not_85_out, not_86_out, not_87_out,
       not_88_out, not_89_out, not_90_out, not_91_out, not_92_out, not_93_out, not_94_out, not_95_out,
       not_96_out, not_97_out, not_98_out, not_99_out, not_100_out, not_101_out, not_102_out, not_103_out,
       not_104_out, not_105_out, not_106_out, not_107_out, not_108_out, not_109_out, not_110_out,
       not_111_out, not_112_out, not_113_out, not_114_out, not_115_out, not_116_out, not_117_out,
       not_118_out, not_119_out, not_120_out, not_121_out, not_122_out, not_123_out, not_124_out,
       not_125_out, not_126_out, not_127_out, not_128_out, not_129_out, not_130_out, not_131_out,
       not_132_out, not_133_out, not_134_out, not_135_out, not_136_out, not_137_out, not_138_out,
       not_139_out, not_140_out, not_141_out, not_142_out, not_143_out, not_144_out, not_145_out,
       not_146_out, not_147_out, not_148_out, or_5_out, or_7_out;

  not not_1 (not_1_out, A0);
  and and_1 (and_1_out, not_1_out, B0);
  and and_2 (and_2_out, A0, not_2_out);
  not not_2 (not_2_out, B0);
  not not_3 (not_3_out, A1);
  not not_4 (not_4_out, A0);
  not not_5 (not_5_out, A1);
  not not_6 (not_6_out, B0);
  not not_7 (not_7_out, A1);
  not not_8 (not_8_out, B1);
  not not_9 (not_9_out, A0);
  not not_10 (not_10_out, B1);
  not not_11 (not_11_out, B1);
  not not_12 (not_12_out, B0);
  not not_13 (not_13_out, A2);
  not not_14 (not_14_out, A1);
  not not_15 (not_15_out, A0);
  not not_16 (not_16_out, A2);
  not not_17 (not_17_out, A1);
  not not_18 (not_18_out, B1);
  not not_19 (not_19_out, A2);
  not not_20 (not_20_out, A1);
  not not_21 (not_21_out, B0);
  not not_22 (not_22_out, A2);
  not not_23 (not_23_out, A0);
  not not_24 (not_24_out, B1);
  not not_25 (not_25_out, A2);
  not not_26 (not_26_out, B1);
  not not_27 (not_27_out, B0);
  not not_28 (not_28_out, A2);
  not not_29 (not_29_out, B2);
  not not_30 (not_30_out, A2);
  not not_31 (not_31_out, B2);
  not not_32 (not_32_out, A2);
  not not_33 (not_33_out, B2);
  not not_34 (not_34_out, A1);
  not not_35 (not_35_out, A0);
  not not_36 (not_36_out, B2);
  not not_37 (not_37_out, A1);
  not not_38 (not_38_out, B2);
  not not_39 (not_39_out, B1);
  not not_40 (not_40_out, A1);
  not not_41 (not_41_out, B2);
  not not_42 (not_42_out, B0);
  not not_43 (not_43_out, A0);
  not not_44 (not_44_out, B2);
  not not_45 (not_45_out, B1);
  not not_46 (not_46_out, B2);
  not not_47 (not_47_out, B1);
  not not_48 (not_48_out, B0);
  not not_49 (not_49_out, A3);
  not not_50 (not_50_out, A2);
  not not_51 (not_51_out, A1);
  not not_52 (not_52_out, A0);
  not not_53 (not_53_out, A3);
  not not_54 (not_54_out, A2);
  not not_55 (not_55_out, A1);
  not not_56 (not_56_out, B1);
  not not_57 (not_57_out, A3);
  not not_58 (not_58_out, A2);
  not not_59 (not_59_out, A1);
  not not_60 (not_60_out, B0);
  not not_61 (not_61_out, A3);
  not not_62 (not_62_out, A2);
  not not_63 (not_63_out, A0);
  not not_64 (not_64_out, B1);
  not not_65 (not_65_out, A3);
  not not_66 (not_66_out, A2);
  not not_67 (not_67_out, B2);
  not not_68 (not_68_out, A3);
  not not_69 (not_69_out, A2);
  not not_70 (not_70_out, B1);
  not not_71 (not_71_out, B0);
  not not_72 (not_72_out, A3);
  not not_73 (not_73_out, A1);
  not not_74 (not_74_out, A0);
  not not_75 (not_75_out, B2);
  not not_76 (not_76_out, A3);
  not not_77 (not_77_out, A1);
  not not_78 (not_78_out, B2);
  not not_79 (not_79_out, B1);
  not not_80 (not_80_out, A3);
  not not_81 (not_81_out, A1);
  not not_82 (not_82_out, B2);
  not not_83 (not_83_out, B0);
  not not_84 (not_84_out, A3);
  not not_85 (not_85_out, A0);
  not not_86 (not_86_out, B2);
  not not_87 (not_87_out, B1);
  not not_88 (not_88_out, A3);
  not not_89 (not_89_out, B2);
  not not_90 (not_90_out, B1);
  not not_91 (not_91_out, B0);
  not not_92 (not_92_out, A3);
  not not_93 (not_93_out, B3);
  not not_94 (not_94_out, A3);
  not not_95 (not_95_out, B3);
  not not_96 (not_96_out, A3);
  not not_97 (not_97_out, B3);
  not not_98 (not_98_out, A3);
  not not_99 (not_99_out, B3);
  not not_100 (not_100_out, A3);
  not not_101 (not_101_out, B3);
  not not_102 (not_102_out, A3);
  not not_103 (not_103_out, B3);
  not not_104 (not_104_out, A3);
  not not_105 (not_105_out, B3);
  not not_106 (not_106_out, A2);
  not not_107 (not_107_out, A1);
  not not_108 (not_108_out, A0);
  not not_109 (not_109_out, B3);
  not not_110 (not_110_out, A2);
  not not_111 (not_111_out, A1);
  not not_112 (not_112_out, B3);
  not not_113 (not_113_out, B1);
  not not_114 (not_114_out, A2);
  not not_115 (not_115_out, A1);
  not not_116 (not_116_out, B3);
  not not_117 (not_117_out, B0);
  not not_118 (not_118_out, A2);
  not not_119 (not_119_out, A0);
  not not_120 (not_120_out, B3);
  not not_121 (not_121_out, B1);
  not not_122 (not_122_out, A2);
  not not_123 (not_123_out, B3);
  not not_124 (not_124_out, B2);
  not not_125 (not_125_out, A2);
  not not_126 (not_126_out, B3);
  not not_127 (not_127_out, B1);
  not not_128 (not_128_out, B0);
  not not_129 (not_129_out, A1);
  not not_130 (not_130_out, A0);
  not not_131 (not_131_out, B3);
  not not_132 (not_132_out, B2);
  not not_133 (not_133_out, A1);
  not not_134 (not_134_out, B3);
  not not_135 (not_135_out, B2);
  not not_136 (not_136_out, B1);
  not not_137 (not_137_out, A1);
  not not_138 (not_138_out, B3);
  not not_139 (not_139_out, B2);
  not not_140 (not_140_out, B0);
  not not_141 (not_141_out, A0);
  not not_142 (not_142_out, B3);
  not not_143 (not_143_out, B2);
  not not_144 (not_144_out, B1);
  not not_145 (not_145_out, B3);
  not not_146 (not_146_out, B2);
  not not_147 (not_147_out, B1);
  not not_148 (not_148_out, B0);
  and and_3 (and_3_out, A0, B3, B2, B1, B0);
  and and_4 (and_4_out, A1, B3, B2, B1);
  and and_5 (and_5_out, A1, A0, B3, B2, B0);
  and and_6 (and_6_out, A2, B3, B2);
  and and_7 (and_7_out, A2, A0, B3, B1, B0);
  and and_8 (and_8_out, A2, A1, B3, B1);
  and and_9 (and_9_out, A2, A1, A0, B3, B0);
  and and_10 (and_10_out, A3, B3);
  and and_11 (and_11_out, A3, A0, B2, B1, B0);
  and and_12 (and_12_out, A3, A1, B2, B1);
  and and_13 (and_13_out, A3, A1, A0, B2, B0);
  and and_14 (and_14_out, A3, A2, B2);
  and and_15 (and_15_out, A3, A2, A0, B1, B0);
  and and_16 (and_16_out, A3, A2, A1, B1);
  and and_17 (and_17_out, A3, A2, A1, A0, B0);
  or or_1 (S0, and_1_out, and_2_out);
  and and_18 (and_18_out, not_3_out, not_4_out, B1);
  and and_19 (and_19_out, not_5_out, B1, not_6_out);
  and and_20 (and_20_out, not_7_out, A0, not_8_out, B0);
  and and_21 (and_21_out, A1, not_9_out, not_10_out);
  and and_22 (and_22_out, A1, not_11_out, not_12_out);
  and and_23 (and_23_out, A1, A0, B1, B0);
  and and_24 (and_24_out, not_13_out, not_14_out, not_15_out, B2);
  and and_25 (and_25_out, not_16_out, not_17_out, B2, not_18_out);
  and and_26 (and_26_out, not_19_out, not_20_out, B2, not_21_out);
  and and_27 (and_27_out, not_22_out, not_23_out, B2, not_24_out);
  and and_28 (and_28_out, not_25_out, B2, not_26_out, not_27_out);
  and and_29 (and_29_out, not_28_out, A0, not_29_out, B1, B0);
  and and_30 (and_30_out, not_30_out, A1, not_31_out, B1);
  and and_31 (and_31_out, not_32_out, A1, A0, not_33_out, B0);
  and and_32 (and_32_out, A2, not_34_out, not_35_out, not_36_out);
  and and_33 (and_33_out, A2, not_37_out, not_38_out, not_39_out);
  and and_34 (and_34_out, A2, not_40_out, not_41_out, not_42_out);
  and and_35 (and_35_out, A2, not_43_out, not_44_out, not_45_out);
  and and_36 (and_36_out, A2, not_46_out, not_47_out, not_48_out);
  and and_37 (and_37_out, A2, A0, B2, B1, B0);
  and and_38 (and_38_out, A2, A1, B2, B1);
  and and_39 (and_39_out, A2, A1, A0, B2, B0);
  and and_40 (and_40_out, not_49_out, not_50_out, not_51_out, not_52_out, B3);
  and and_41 (and_41_out, not_53_out, not_54_out, not_55_out, B3, not_56_out);
  and and_42 (and_42_out, not_57_out, not_58_out, not_59_out, B3, not_60_out);
  and and_43 (and_43_out, not_61_out, not_62_out, not_63_out, B3, not_64_out);
  and and_44 (and_44_out, not_65_out, not_66_out, B3, not_67_out);
  and and_45 (and_45_out, not_68_out, not_69_out, B3, not_70_out, not_71_out);
  and and_46 (and_46_out, not_72_out, not_73_out, not_74_out, B3, not_75_out);
  and and_47 (and_47_out, not_76_out, not_77_out, B3, not_78_out, not_79_out);
  and and_48 (and_48_out, not_80_out, not_81_out, B3, not_82_out, not_83_out);
  and and_49 (and_49_out, not_84_out, not_85_out, B3, not_86_out, not_87_out);
  and and_50 (and_50_out, not_88_out, B3, not_89_out, not_90_out, not_91_out);
  and and_51 (and_51_out, not_92_out, A0, not_93_out, B2, B1, B0);
  and and_52 (and_52_out, not_94_out, A1, not_95_out, B2, B1);
  and and_53 (and_53_out, not_96_out, A1, A0, not_97_out, B2, B0);
  and and_54 (and_54_out, not_98_out, A2, not_99_out, B2);
  and and_55 (and_55_out, not_100_out, A2, A0, not_101_out, B1, B0);
  and and_56 (and_56_out, not_102_out, A2, A1, not_103_out, B1);
  and and_57 (and_57_out, not_104_out, A2, A1, A0, not_105_out, B0);
  and and_58 (and_58_out, A3, not_106_out, not_107_out, not_108_out, not_109_out);
  and and_59 (and_59_out, A3, not_110_out, not_111_out, not_112_out, not_113_out);
  and and_60 (and_60_out, A3, not_114_out, not_115_out, not_116_out, not_117_out);
  and and_61 (and_61_out, A3, not_118_out, not_119_out, not_120_out, not_121_out);
  and and_62 (and_62_out, A3, not_122_out, not_123_out, not_124_out);
  and and_63 (and_63_out, A3, not_125_out, not_126_out, not_127_out, not_128_out);
  and and_64 (and_64_out, A3, not_129_out, not_130_out, not_131_out, not_132_out);
  and and_65 (and_65_out, A3, not_133_out, not_134_out, not_135_out, not_136_out);
  and and_66 (and_66_out, A3, not_137_out, not_138_out, not_139_out, not_140_out);
  and and_67 (and_67_out, A3, not_141_out, not_142_out, not_143_out, not_144_out);
  and and_68 (and_68_out, A3, not_145_out, not_146_out, not_147_out, not_148_out);
  and and_69 (and_69_out, A3, A0, B3, B2, B1, B0);
  and and_70 (and_70_out, A3, A1, B3, B2, B1);
  and and_71 (and_71_out, A3, A1, A0, B3, B2, B0);
  and and_72 (and_72_out, A3, A2, B3, B2);
  and and_73 (and_73_out, A3, A2, A0, B3, B1, B0);
  and and_74 (and_74_out, A3, A2, A1, B3, B1);
  and and_75 (and_75_out, A3, A2, A1, A0, B3, B0);
  or or_2 (S4, and_3_out, and_4_out, and_5_out, and_6_out, and_7_out, and_8_out, and_9_out, and_10_out, and_11_out, and_12_out, and_13_out, and_14_out, and_15_out, and_16_out, and_17_out);
  or or_3 (S1, and_18_out, and_19_out, and_20_out, and_21_out, and_22_out, and_23_out);
  or or_4 (S2, and_24_out, and_25_out, and_26_out, and_27_out, and_28_out, and_29_out, and_30_out, and_31_out, and_32_out, and_33_out, and_34_out, and_35_out, and_36_out, and_37_out, and_38_out, and_39_out);
  or or_5 (or_5_out, and_40_out, and_41_out, and_42_out, and_43_out, and_44_out, and_45_out, and_46_out, and_47_out, and_48_out, and_49_out, and_50_out, and_51_out, and_52_out, and_53_out, and_54_out, and_55_out, and_56_out, and_57_out);
  or or_6 (S3, or_5_out, or_7_out);
  or or_7 (or_7_out, and_58_out, and_59_out, and_60_out, and_61_out, and_62_out, and_63_out, and_64_out, and_65_out, and_66_out, and_67_out, and_68_out, and_69_out, and_70_out, and_71_out, and_72_out, and_73_out, and_74_out, and_75_out);
endmodule

module subtrator (
  input  A3,
  input  A2,
  input  A1,
  input  A0,
  input  B3,
  input  B2,
  input  B1,
  input  B0,
  output S0,
  output S1,
  output S2,
  output S3,
  output Ov
);

  wire and_1_out, and_2_out, and_3_out, and_4_out, and_5_out, and_6_out, and_7_out, and_8_out, and_9_out,
       and_10_out, and_11_out, and_12_out, and_13_out, and_14_out, and_15_out, and_16_out, and_17_out,
       and_18_out, and_19_out, and_20_out, and_21_out, and_22_out, and_23_out, and_24_out, and_25_out,
       and_26_out, and_27_out, and_28_out, and_29_out, and_30_out, and_31_out, and_32_out, and_33_out,
       and_34_out, and_35_out, and_36_out, and_37_out, and_38_out, and_39_out, and_40_out, and_41_out,
       and_42_out, and_43_out, and_44_out, and_45_out, and_46_out, and_47_out, and_48_out, and_49_out,
       and_50_out, and_51_out, and_52_out, and_53_out, and_54_out, and_55_out, and_56_out, and_57_out,
       and_58_out, and_59_out, and_60_out, and_61_out, and_62_out, and_63_out, and_64_out, and_65_out,
       and_66_out, and_67_out, and_68_out, and_69_out, and_70_out, and_71_out, and_72_out, and_73_out,
       and_74_out, and_75_out, not_1_out, not_2_out, not_3_out, not_4_out, not_5_out, not_6_out, not_7_out,
       not_8_out, not_9_out, not_10_out, not_11_out, not_12_out, not_13_out, not_14_out, not_15_out,
       not_16_out, not_17_out, not_18_out, not_19_out, not_20_out, not_21_out, not_22_out, not_23_out,
       not_24_out, not_25_out, not_26_out, not_27_out, not_28_out, not_29_out, not_30_out, not_31_out,
       not_32_out, not_33_out, not_34_out, not_35_out, not_36_out, not_37_out, not_38_out, not_39_out,
       not_40_out, not_41_out, not_42_out, not_43_out, not_44_out, not_45_out, not_46_out, not_47_out,
       not_48_out, not_49_out, not_50_out, not_51_out, not_52_out, not_53_out, not_54_out, not_55_out,
       not_56_out, not_57_out, not_58_out, not_59_out, not_60_out, not_61_out, not_62_out, not_63_out,
       not_64_out, not_65_out, not_66_out, not_67_out, not_68_out, not_69_out, not_70_out, not_71_out,
       not_72_out, not_73_out, not_74_out, not_75_out, not_76_out, not_77_out, not_78_out, not_79_out,
       not_80_out, not_81_out, not_82_out, not_83_out, not_84_out, not_85_out, not_86_out, not_87_out,
       not_88_out, not_89_out, not_90_out, not_91_out, not_92_out, not_93_out, not_94_out, not_95_out,
       not_96_out, not_97_out, not_98_out, not_99_out, not_100_out, not_101_out, not_102_out, not_103_out,
       not_104_out, not_105_out, not_106_out, not_107_out, not_108_out, not_109_out, not_110_out,
       not_111_out, not_112_out, not_113_out, not_114_out, not_115_out, not_116_out, not_117_out,
       not_118_out, not_119_out, not_120_out, not_121_out, not_122_out, not_123_out, not_124_out,
       not_125_out, not_126_out, not_127_out, not_128_out, not_129_out, not_130_out, not_131_out,
       not_132_out, not_133_out, not_134_out, not_135_out, not_136_out, not_137_out, not_138_out,
       not_139_out, not_140_out, not_141_out, not_142_out, not_143_out, not_144_out, not_145_out,
       not_146_out, not_147_out, not_148_out, not_149_out, not_150_out, not_151_out, not_152_out,
       not_153_out, not_154_out, not_155_out, not_156_out, not_157_out, not_158_out, not_159_out,
       not_160_out, not_161_out, not_162_out, not_163_out, not_164_out, not_165_out, not_166_out,
       not_167_out, not_168_out, not_169_out, not_170_out, or_5_out, or_7_out;

  not not_1 (not_1_out, A0);
  and and_1 (and_1_out, not_1_out, B0);
  and and_2 (and_2_out, A0, not_2_out);
  not not_2 (not_2_out, B0);
  not not_3 (not_3_out, A1);
  not not_4 (not_4_out, A0);
  not not_5 (not_5_out, B1);
  not not_6 (not_6_out, A1);
  not not_7 (not_7_out, B0);
  not not_8 (not_8_out, A1);
  not not_9 (not_9_out, B1);
  not not_10 (not_10_out, B0);
  not not_11 (not_11_out, A0);
  not not_12 (not_12_out, B1);
  not not_13 (not_13_out, A2);
  not not_14 (not_14_out, A1);
  not not_15 (not_15_out, A0);
  not not_16 (not_16_out, B2);
  not not_17 (not_17_out, A2);
  not not_18 (not_18_out, A1);
  not not_19 (not_19_out, B2);
  not not_20 (not_20_out, A2);
  not not_21 (not_21_out, A0);
  not not_22 (not_22_out, B2);
  not not_23 (not_23_out, A2);
  not not_24 (not_24_out, B1);
  not not_25 (not_25_out, B0);
  not not_26 (not_26_out, A2);
  not not_27 (not_27_out, B1);
  not not_28 (not_28_out, A2);
  not not_29 (not_29_out, B1);
  not not_30 (not_30_out, A2);
  not not_31 (not_31_out, B0);
  not not_32 (not_32_out, A2);
  not not_33 (not_33_out, B2);
  not not_34 (not_34_out, B1);
  not not_35 (not_35_out, B0);
  not not_36 (not_36_out, A1);
  not not_37 (not_37_out, A0);
  not not_38 (not_38_out, A1);
  not not_39 (not_39_out, A0);
  not not_40 (not_40_out, B2);
  not not_41 (not_41_out, B1);
  not not_42 (not_42_out, B2);
  not not_43 (not_43_out, B1);
  not not_44 (not_44_out, B2);
  not not_45 (not_45_out, B0);
  not not_46 (not_46_out, B2);
  not not_47 (not_47_out, A3);
  not not_48 (not_48_out, A2);
  not not_49 (not_49_out, A1);
  not not_50 (not_50_out, A0);
  not not_51 (not_51_out, B3);
  not not_52 (not_52_out, A3);
  not not_53 (not_53_out, A2);
  not not_54 (not_54_out, A1);
  not not_55 (not_55_out, B3);
  not not_56 (not_56_out, A3);
  not not_57 (not_57_out, A2);
  not not_58 (not_58_out, A0);
  not not_59 (not_59_out, B3);
  not not_60 (not_60_out, A3);
  not not_61 (not_61_out, A2);
  not not_62 (not_62_out, B3);
  not not_63 (not_63_out, A3);
  not not_64 (not_64_out, A1);
  not not_65 (not_65_out, A0);
  not not_66 (not_66_out, B3);
  not not_67 (not_67_out, A3);
  not not_68 (not_68_out, A1);
  not not_69 (not_69_out, B3);
  not not_70 (not_70_out, A3);
  not not_71 (not_71_out, A0);
  not not_72 (not_72_out, B3);
  not not_73 (not_73_out, A3);
  not not_74 (not_74_out, B2);
  not not_75 (not_75_out, B1);
  not not_76 (not_76_out, B0);
  not not_77 (not_77_out, A3);
  not not_78 (not_78_out, B2);
  not not_79 (not_79_out, B1);
  not not_80 (not_80_out, A3);
  not not_81 (not_81_out, B2);
  not not_82 (not_82_out, B1);
  not not_83 (not_83_out, A3);
  not not_84 (not_84_out, B2);
  not not_85 (not_85_out, B0);
  not not_86 (not_86_out, A3);
  not not_87 (not_87_out, B2);
  not not_88 (not_88_out, A3);
  not not_89 (not_89_out, B2);
  not not_90 (not_90_out, A3);
  not not_91 (not_91_out, B1);
  not not_92 (not_92_out, B0);
  not not_93 (not_93_out, A3);
  not not_94 (not_94_out, B1);
  not not_95 (not_95_out, A3);
  not not_96 (not_96_out, B1);
  not not_97 (not_97_out, A3);
  not not_98 (not_98_out, B0);
  not not_99 (not_99_out, A3);
  not not_100 (not_100_out, B3);
  not not_101 (not_101_out, B2);
  not not_102 (not_102_out, B1);
  not not_103 (not_103_out, B0);
  not not_104 (not_104_out, A2);
  not not_105 (not_105_out, A1);
  not not_106 (not_106_out, A0);
  not not_107 (not_107_out, A2);
  not not_108 (not_108_out, A1);
  not not_109 (not_109_out, A2);
  not not_110 (not_110_out, A0);
  not not_111 (not_111_out, A2);
  not not_112 (not_112_out, A1);
  not not_113 (not_113_out, A0);
  not not_114 (not_114_out, A1);
  not not_115 (not_115_out, A0);
  not not_116 (not_116_out, B3);
  not not_117 (not_117_out, B2);
  not not_118 (not_118_out, B1);
  not not_119 (not_119_out, B3);
  not not_120 (not_120_out, B2);
  not not_121 (not_121_out, B1);
  not not_122 (not_122_out, B3);
  not not_123 (not_123_out, B2);
  not not_124 (not_124_out, B0);
  not not_125 (not_125_out, B3);
  not not_126 (not_126_out, B2);
  not not_127 (not_127_out, B3);
  not not_128 (not_128_out, B2);
  not not_129 (not_129_out, B3);
  not not_130 (not_130_out, B1);
  not not_131 (not_131_out, B0);
  not not_132 (not_132_out, B3);
  not not_133 (not_133_out, B1);
  not not_134 (not_134_out, B3);
  not not_135 (not_135_out, B1);
  not not_136 (not_136_out, B3);
  not not_137 (not_137_out, B0);
  not not_138 (not_138_out, B3);
  not not_139 (not_139_out, A3);
  not not_140 (not_140_out, A2);
  not not_141 (not_141_out, A1);
  not not_142 (not_142_out, A0);
  not not_143 (not_143_out, A3);
  not not_144 (not_144_out, A2);
  not not_145 (not_145_out, A1);
  not not_146 (not_146_out, A3);
  not not_147 (not_147_out, A2);
  not not_148 (not_148_out, A0);
  not not_149 (not_149_out, A3);
  not not_150 (not_150_out, A2);
  not not_151 (not_151_out, A3);
  not not_152 (not_152_out, A1);
  not not_153 (not_153_out, A0);
  not not_154 (not_154_out, A3);
  not not_155 (not_155_out, A1);
  not not_156 (not_156_out, A3);
  not not_157 (not_157_out, A0);
  not not_158 (not_158_out, A3);
  not not_159 (not_159_out, A2);
  not not_160 (not_160_out, A1);
  not not_161 (not_161_out, A0);
  not not_162 (not_162_out, A2);
  not not_163 (not_163_out, A1);
  not not_164 (not_164_out, A2);
  not not_165 (not_165_out, A0);
  not not_166 (not_166_out, A2);
  not not_167 (not_167_out, A1);
  not not_168 (not_168_out, A0);
  not not_169 (not_169_out, A1);
  not not_170 (not_170_out, A0);
  or or_1 (S0, and_1_out, and_2_out);
  and and_3 (and_3_out, not_3_out, not_4_out, not_5_out, B0);
  and and_4 (and_4_out, not_6_out, B1, not_7_out);
  and and_5 (and_5_out, not_8_out, A0, B1);
  and and_6 (and_6_out, A1, not_9_out, not_10_out);
  and and_7 (and_7_out, A1, not_11_out, B1, B0);
  and and_8 (and_8_out, A1, A0, not_12_out);
  and and_9 (and_9_out, not_13_out, not_14_out, not_15_out, not_16_out, B0);
  and and_10 (and_10_out, not_17_out, not_18_out, not_19_out, B1);
  and and_11 (and_11_out, not_20_out, not_21_out, not_22_out, B1, B0);
  and and_12 (and_12_out, not_23_out, B2, not_24_out, not_25_out);
  and and_13 (and_13_out, not_26_out, A0, B2, not_27_out);
  and and_14 (and_14_out, not_28_out, A1, B2, not_29_out);
  and and_15 (and_15_out, not_30_out, A1, B2, not_31_out);
  and and_16 (and_16_out, not_32_out, A1, A0, B2);
  and and_17 (and_17_out, A2, not_33_out, not_34_out, not_35_out);
  and and_18 (and_18_out, A2, not_36_out, not_37_out, B2, B0);
  and and_19 (and_19_out, A2, not_38_out, B2, B1);
  and and_20 (and_20_out, A2, not_39_out, B2, B1, B0);
  and and_21 (and_21_out, A2, A0, not_40_out, not_41_out);
  and and_22 (and_22_out, A2, A1, not_42_out, not_43_out);
  and and_23 (and_23_out, A2, A1, not_44_out, not_45_out);
  and and_24 (and_24_out, A2, A1, A0, not_46_out);
  and and_25 (and_25_out, not_47_out, not_48_out, not_49_out, not_50_out, not_51_out, B0);
  and and_26 (and_26_out, not_52_out, not_53_out, not_54_out, not_55_out, B1);
  and and_27 (and_27_out, not_56_out, not_57_out, not_58_out, not_59_out, B1, B0);
  and and_28 (and_28_out, not_60_out, not_61_out, not_62_out, B2);
  and and_29 (and_29_out, not_63_out, not_64_out, not_65_out, not_66_out, B2, B0);
  and and_30 (and_30_out, not_67_out, not_68_out, not_69_out, B2, B1);
  and and_31 (and_31_out, not_70_out, not_71_out, not_72_out, B2, B1, B0);
  and and_32 (and_32_out, not_73_out, B3, not_74_out, not_75_out, not_76_out);
  and and_33 (and_33_out, not_77_out, A0, B3, not_78_out, not_79_out);
  and and_34 (and_34_out, not_80_out, A1, B3, not_81_out, not_82_out);
  and and_35 (and_35_out, not_83_out, A1, B3, not_84_out, not_85_out);
  and and_36 (and_36_out, not_86_out, A1, A0, B3, not_87_out);
  and and_37 (and_37_out, not_88_out, A2, B3, not_89_out);
  and and_38 (and_38_out, not_90_out, A2, B3, not_91_out, not_92_out);
  and and_39 (and_39_out, not_93_out, A2, A0, B3, not_94_out);
  and and_40 (and_40_out, not_95_out, A2, A1, B3, not_96_out);
  and and_41 (and_41_out, not_97_out, A2, A1, B3, not_98_out);
  and and_42 (and_42_out, not_99_out, A2, A1, A0, B3);
  and and_43 (and_43_out, A3, not_100_out, not_101_out, not_102_out, not_103_out);
  and and_44 (and_44_out, A3, not_104_out, not_105_out, not_106_out, B3, B0);
  and and_45 (and_45_out, A3, not_107_out, not_108_out, B3, B1);
  and and_46 (and_46_out, A3, not_109_out, not_110_out, B3, B1, B0);
  and and_47 (and_47_out, A3, not_111_out, B3, B2);
  and and_48 (and_48_out, A3, not_112_out, not_113_out, B3, B2, B0);
  and and_49 (and_49_out, A3, not_114_out, B3, B2, B1);
  and and_50 (and_50_out, A3, not_115_out, B3, B2, B1, B0);
  and and_51 (and_51_out, A3, A0, not_116_out, not_117_out, not_118_out);
  and and_52 (and_52_out, A3, A1, not_119_out, not_120_out, not_121_out);
  and and_53 (and_53_out, A3, A1, not_122_out, not_123_out, not_124_out);
  and and_54 (and_54_out, A3, A1, A0, not_125_out, not_126_out);
  and and_55 (and_55_out, A3, A2, not_127_out, not_128_out);
  and and_56 (and_56_out, A3, A2, not_129_out, not_130_out, not_131_out);
  and and_57 (and_57_out, A3, A2, A0, not_132_out, not_133_out);
  and and_58 (and_58_out, A3, A2, A1, not_134_out, not_135_out);
  and and_59 (and_59_out, A3, A2, A1, not_136_out, not_137_out);
  and and_60 (and_60_out, A3, A2, A1, A0, not_138_out);
  and and_61 (and_61_out, not_139_out, not_140_out, not_141_out, not_142_out, B0);
  and and_62 (and_62_out, not_143_out, not_144_out, not_145_out, B1);
  and and_63 (and_63_out, not_146_out, not_147_out, not_148_out, B1, B0);
  and and_64 (and_64_out, not_149_out, not_150_out, B2);
  and and_65 (and_65_out, not_151_out, not_152_out, not_153_out, B2, B0);
  and and_66 (and_66_out, not_154_out, not_155_out, B2, B1);
  and and_67 (and_67_out, not_156_out, not_157_out, B2, B1, B0);
  and and_68 (and_68_out, not_158_out, B3);
  and and_69 (and_69_out, not_159_out, not_160_out, not_161_out, B3, B0);
  and and_70 (and_70_out, not_162_out, not_163_out, B3, B1);
  and and_71 (and_71_out, not_164_out, not_165_out, B3, B1, B0);
  and and_72 (and_72_out, not_166_out, B3, B2);
  and and_73 (and_73_out, not_167_out, not_168_out, B3, B2, B0);
  and and_74 (and_74_out, not_169_out, B3, B2, B1);
  and and_75 (and_75_out, not_170_out, B3, B2, B1, B0);
  or or_2 (S1, and_3_out, and_4_out, and_5_out, and_6_out, and_7_out, and_8_out);
  or or_3 (S2, and_9_out, and_10_out, and_11_out, and_12_out, and_13_out, and_14_out, and_15_out, and_16_out, and_17_out, and_18_out, and_19_out, and_20_out, and_21_out, and_22_out, and_23_out, and_24_out);
  or or_4 (Ov, and_61_out, and_62_out, and_63_out, and_64_out, and_65_out, and_66_out, and_67_out, and_68_out, and_69_out, and_70_out, and_71_out, and_72_out, and_73_out, and_74_out, and_75_out);
  or or_5 (or_5_out, and_25_out, and_26_out, and_27_out, and_28_out, and_29_out, and_30_out, and_31_out, and_32_out, and_33_out, and_34_out, and_35_out, and_36_out, and_37_out, and_38_out, and_39_out, and_40_out, and_41_out, and_42_out);
  or or_6 (S3, or_5_out, or_7_out);
  or or_7 (or_7_out, and_43_out, and_44_out, and_45_out, and_46_out, and_47_out, and_48_out, and_49_out, and_50_out, and_51_out, and_52_out, and_53_out, and_54_out, and_55_out, and_56_out, and_57_out, and_58_out, and_59_out, and_60_out);
endmodule

module ad_sub_dmx (
  input  A0,
  input  A1,
  input  A2,
  input  A3,
  input  B0,
  input  B1,
  input  B2,
  input  B3,
  input  AdSub,
  output S0,
  output S1,
  output S2,
  output S3,
  output Overflow
);

  wire and_1_out, and_2_out, and_3_out, and_4_out, and_5_out, and_6_out, and_7_out, and_8_out, and_9_out,
       and_10_out, and_11_out, and_12_out, and_13_out, and_14_out, and_15_out, and_16_out, and_17_out,
       and_18_out, and_19_out, and_20_out, and_21_out, and_22_out, and_23_out, and_24_out, and_25_out,
       and_26_out, and_27_out, and_28_out, and_29_out, and_30_out, and_31_out, and_32_out, and_33_out,
       and_34_out, and_35_out, and_36_out, and_37_out, and_38_out, and_39_out, and_40_out, and_41_out,
       and_42_out, and_43_out, and_44_out, and_45_out, and_46_out, and_47_out, and_48_out, and_49_out,
       and_50_out, and_51_out, and_52_out, and_53_out, and_54_out, and_55_out, and_56_out, and_57_out,
       and_58_out, and_59_out, and_60_out, and_61_out, and_62_out, and_63_out, and_64_out, and_65_out,
       and_66_out, and_67_out, and_68_out, and_69_out, and_70_out, and_71_out, and_72_out, and_73_out,
       and_74_out, and_75_out, and_76_out, and_77_out, and_78_out, and_79_out, and_80_out, and_81_out,
       and_82_out, and_83_out, and_84_out, and_85_out, and_86_out, and_87_out, and_88_out, and_89_out,
       and_90_out, and_91_out, and_92_out, and_93_out, and_94_out, and_95_out, and_96_out, and_97_out,
       and_98_out, and_99_out, and_100_out, and_101_out, and_102_out, and_103_out, and_104_out, and_105_out,
       and_106_out, and_107_out, and_108_out, and_109_out, and_110_out, and_111_out, and_112_out,
       and_113_out, and_114_out, and_115_out, and_116_out, and_117_out, and_118_out, and_119_out,
       and_120_out, and_121_out, and_122_out, and_123_out, and_124_out, and_125_out, and_126_out,
       and_127_out, and_128_out, and_129_out, and_130_out, and_131_out, and_132_out, and_133_out,
       and_134_out, not_1_out, not_2_out, not_3_out, not_4_out, not_5_out, not_6_out, not_7_out, not_8_out,
       not_9_out, not_10_out, not_11_out, not_12_out, not_13_out, not_14_out, not_15_out, not_16_out,
       not_17_out, not_18_out, not_19_out, not_20_out, not_21_out, not_22_out, not_23_out, not_24_out,
       not_25_out, not_26_out, not_27_out, not_28_out, not_29_out, not_30_out, not_31_out, not_32_out,
       not_33_out, not_34_out, not_35_out, not_36_out, not_37_out, not_38_out, not_39_out, not_40_out,
       not_41_out, not_42_out, not_43_out, not_44_out, not_45_out, not_46_out, not_47_out, not_48_out,
       not_49_out, not_50_out, not_51_out, not_52_out, not_53_out, not_54_out, not_55_out, not_56_out,
       not_57_out, not_58_out, not_59_out, not_60_out, not_61_out, not_62_out, not_63_out, not_64_out,
       not_65_out, not_66_out, not_67_out, not_68_out, not_69_out, not_70_out, not_71_out, not_72_out,
       not_73_out, not_74_out, not_75_out, not_76_out, not_77_out, not_78_out, not_79_out, not_80_out,
       not_81_out, not_82_out, not_83_out, not_84_out, not_85_out, not_86_out, not_87_out, not_88_out,
       not_89_out, not_90_out, not_91_out, not_92_out, not_93_out, not_94_out, not_95_out, not_96_out,
       not_97_out, not_98_out, not_99_out, not_100_out, not_101_out, not_102_out, not_103_out, not_104_out,
       not_105_out, not_106_out, not_107_out, not_108_out, not_109_out, not_110_out, not_111_out,
       not_112_out, not_113_out, not_114_out, not_115_out, not_116_out, not_117_out, not_118_out,
       not_119_out, not_120_out, not_121_out, not_122_out, not_123_out, not_124_out, not_125_out,
       not_126_out, not_127_out, not_128_out, not_129_out, not_130_out, not_131_out, not_132_out,
       not_133_out, not_134_out, not_135_out, not_136_out, not_137_out, not_138_out, not_139_out,
       not_140_out, not_141_out, not_142_out, not_143_out, not_144_out, not_145_out, not_146_out,
       not_147_out, not_148_out, not_149_out, not_150_out, not_151_out, not_152_out, not_153_out,
       not_154_out, not_155_out, not_156_out, not_157_out, not_158_out, not_159_out, not_160_out,
       not_161_out, not_162_out, not_163_out, not_164_out, not_165_out, not_166_out, not_167_out,
       not_168_out, not_169_out, not_170_out, not_171_out, not_172_out, not_173_out, not_174_out,
       not_175_out, not_176_out, not_177_out, not_178_out, not_179_out, not_180_out, not_181_out,
       not_182_out, not_183_out, not_184_out, not_185_out, not_186_out, not_187_out, not_188_out,
       not_189_out, not_190_out, not_191_out, not_192_out, not_193_out, not_194_out, not_195_out,
       not_196_out, not_197_out, not_198_out, not_199_out, not_200_out, not_201_out, not_202_out,
       not_203_out, not_204_out, not_205_out, not_206_out, not_207_out, not_208_out, not_209_out,
       not_210_out, not_211_out, not_212_out, not_213_out, not_214_out, not_215_out, not_216_out,
       not_217_out, not_218_out, not_219_out, not_220_out, not_221_out, not_222_out, not_223_out,
       not_224_out, not_225_out, not_226_out, not_227_out, not_228_out, not_229_out, not_230_out,
       not_231_out, not_232_out, not_233_out, not_234_out, not_235_out, not_236_out, not_237_out,
       not_238_out, not_239_out, not_240_out, not_241_out, not_242_out, not_243_out, not_244_out,
       not_245_out, not_246_out, not_247_out, not_248_out, not_249_out, not_250_out, not_251_out,
       not_252_out, not_253_out, not_254_out, not_255_out, not_256_out, not_257_out, not_258_out,
       not_259_out, not_260_out, not_261_out, not_262_out, not_263_out, not_264_out, not_265_out,
       not_266_out, not_267_out, not_268_out, not_269_out, not_270_out, not_271_out, not_272_out,
       not_273_out, not_274_out, not_275_out, not_276_out, not_277_out, not_278_out, not_279_out,
       not_280_out, not_281_out, not_282_out, not_283_out, not_284_out, not_285_out, not_286_out,
       not_287_out, not_288_out, not_289_out, not_290_out, not_291_out, not_292_out, not_293_out,
       not_294_out, not_295_out, not_296_out, not_297_out, not_298_out, not_299_out, not_300_out,
       not_301_out, not_302_out, not_303_out, not_304_out, not_305_out, not_306_out, not_307_out,
       not_308_out, not_309_out, not_310_out, not_311_out, not_312_out, not_313_out, not_314_out,
       not_315_out, not_316_out, not_317_out, not_318_out, not_319_out, not_320_out, not_321_out,
       not_322_out, not_323_out, not_324_out, not_325_out, not_326_out, not_327_out, not_328_out,
       not_329_out, not_330_out, not_331_out, not_332_out, not_333_out, not_334_out, not_335_out,
       not_336_out, not_337_out, not_338_out, not_339_out, not_340_out, not_341_out, or_4_out, or_5_out,
       or_6_out;

  not not_1 (not_1_out, A0);
  not not_2 (not_2_out, B0);
  not not_3 (not_3_out, A0);
  not not_4 (not_4_out, A1);
  not not_5 (not_5_out, AdSub);
  not not_6 (not_6_out, A1);
  not not_7 (not_7_out, B0);
  not not_8 (not_8_out, A0);
  not not_9 (not_9_out, A1);
  not not_10 (not_10_out, B1);
  not not_11 (not_11_out, A0);
  not not_12 (not_12_out, B1);
  not not_13 (not_13_out, AdSub);
  not not_14 (not_14_out, B0);
  not not_15 (not_15_out, B1);
  not not_16 (not_16_out, A0);
  not not_17 (not_17_out, A1);
  not not_18 (not_18_out, A1);
  not not_19 (not_19_out, B1);
  not not_20 (not_20_out, AdSub);
  not not_21 (not_21_out, B1);
  not not_22 (not_22_out, AdSub);
  not not_23 (not_23_out, A0);
  not not_24 (not_24_out, A1);
  not not_25 (not_25_out, A2);
  not not_26 (not_26_out, AdSub);
  not not_27 (not_27_out, A1);
  not not_28 (not_28_out, A2);
  not not_29 (not_29_out, B0);
  not not_30 (not_30_out, AdSub);
  not not_31 (not_31_out, A2);
  not not_32 (not_32_out, B0);
  not not_33 (not_33_out, B1);
  not not_34 (not_34_out, A1);
  not not_35 (not_35_out, A2);
  not not_36 (not_36_out, B2);
  not not_37 (not_37_out, A0);
  not not_38 (not_38_out, A1);
  not not_39 (not_39_out, A2);
  not not_40 (not_40_out, B2);
  not not_41 (not_41_out, A0);
  not not_42 (not_42_out, A1);
  not not_43 (not_43_out, B2);
  not not_44 (not_44_out, AdSub);
  not not_45 (not_45_out, A1);
  not not_46 (not_46_out, B0);
  not not_47 (not_47_out, B2);
  not not_48 (not_48_out, AdSub);
  not not_49 (not_49_out, B0);
  not not_50 (not_50_out, B1);
  not not_51 (not_51_out, B2);
  not not_52 (not_52_out, A1);
  not not_53 (not_53_out, A0);
  not not_54 (not_54_out, A1);
  not not_55 (not_55_out, A0);
  not not_56 (not_56_out, A2);
  not not_57 (not_57_out, B1);
  not not_58 (not_58_out, A2);
  not not_59 (not_59_out, B0);
  not not_60 (not_60_out, A2);
  not not_61 (not_61_out, B2);
  not not_62 (not_62_out, AdSub);
  not not_63 (not_63_out, A0);
  not not_64 (not_64_out, A2);
  not not_65 (not_65_out, B2);
  not not_66 (not_66_out, A0);
  not not_67 (not_67_out, B1);
  not not_68 (not_68_out, B2);
  not not_69 (not_69_out, B0);
  not not_70 (not_70_out, B2);
  not not_71 (not_71_out, AdSub);
  not not_72 (not_72_out, A0);
  not not_73 (not_73_out, A1);
  not not_74 (not_74_out, A2);
  not not_75 (not_75_out, B1);
  not not_76 (not_76_out, A2);
  not not_77 (not_77_out, B2);
  not not_78 (not_78_out, AdSub);
  not not_79 (not_79_out, A1);
  not not_80 (not_80_out, B1);
  not not_81 (not_81_out, B2);
  not not_82 (not_82_out, AdSub);
  not not_83 (not_83_out, A2);
  not not_84 (not_84_out, A2);
  not not_85 (not_85_out, B2);
  not not_86 (not_86_out, AdSub);
  not not_87 (not_87_out, B2);
  not not_88 (not_88_out, AdSub);
  not not_89 (not_89_out, A0);
  not not_90 (not_90_out, A1);
  not not_91 (not_91_out, A2);
  not not_92 (not_92_out, A3);
  not not_93 (not_93_out, AdSub);
  not not_94 (not_94_out, A0);
  not not_95 (not_95_out, A1);
  not not_96 (not_96_out, A3);
  not not_97 (not_97_out, B2);
  not not_98 (not_98_out, AdSub);
  not not_99 (not_99_out, A0);
  not not_100 (not_100_out, A2);
  not not_101 (not_101_out, A3);
  not not_102 (not_102_out, B1);
  not not_103 (not_103_out, AdSub);
  not not_104 (not_104_out, A1);
  not not_105 (not_105_out, A2);
  not not_106 (not_106_out, A3);
  not not_107 (not_107_out, B0);
  not not_108 (not_108_out, AdSub);
  not not_109 (not_109_out, A1);
  not not_110 (not_110_out, A2);
  not not_111 (not_111_out, A3);
  not not_112 (not_112_out, B1);
  not not_113 (not_113_out, AdSub);
  not not_114 (not_114_out, A1);
  not not_115 (not_115_out, A3);
  not not_116 (not_116_out, B0);
  not not_117 (not_117_out, B2);
  not not_118 (not_118_out, AdSub);
  not not_119 (not_119_out, A2);
  not not_120 (not_120_out, A3);
  not not_121 (not_121_out, B0);
  not not_122 (not_122_out, B1);
  not not_123 (not_123_out, AdSub);
  not not_124 (not_124_out, A2);
  not not_125 (not_125_out, A3);
  not not_126 (not_126_out, B2);
  not not_127 (not_127_out, AdSub);
  not not_128 (not_128_out, A3);
  not not_129 (not_129_out, B0);
  not not_130 (not_130_out, B1);
  not not_131 (not_131_out, B2);
  not not_132 (not_132_out, A2);
  not not_133 (not_133_out, A3);
  not not_134 (not_134_out, B3);
  not not_135 (not_135_out, A1);
  not not_136 (not_136_out, A2);
  not not_137 (not_137_out, A3);
  not not_138 (not_138_out, B3);
  not not_139 (not_139_out, A1);
  not not_140 (not_140_out, A3);
  not not_141 (not_141_out, B3);
  not not_142 (not_142_out, A0);
  not not_143 (not_143_out, A1);
  not not_144 (not_144_out, A2);
  not not_145 (not_145_out, A3);
  not not_146 (not_146_out, B3);
  not not_147 (not_147_out, A0);
  not not_148 (not_148_out, A1);
  not not_149 (not_149_out, A3);
  not not_150 (not_150_out, B3);
  not not_151 (not_151_out, A0);
  not not_152 (not_152_out, A2);
  not not_153 (not_153_out, A3);
  not not_154 (not_154_out, B3);
  not not_155 (not_155_out, A0);
  not not_156 (not_156_out, A1);
  not not_157 (not_157_out, A2);
  not not_158 (not_158_out, B3);
  not not_159 (not_159_out, AdSub);
  not not_160 (not_160_out, A0);
  not not_161 (not_161_out, A1);
  not not_162 (not_162_out, B2);
  not not_163 (not_163_out, B3);
  not not_164 (not_164_out, AdSub);
  not not_165 (not_165_out, A0);
  not not_166 (not_166_out, A2);
  not not_167 (not_167_out, B1);
  not not_168 (not_168_out, B3);
  not not_169 (not_169_out, AdSub);
  not not_170 (not_170_out, A1);
  not not_171 (not_171_out, A2);
  not not_172 (not_172_out, B0);
  not not_173 (not_173_out, B3);
  not not_174 (not_174_out, AdSub);
  not not_175 (not_175_out, A1);
  not not_176 (not_176_out, A2);
  not not_177 (not_177_out, B1);
  not not_178 (not_178_out, B3);
  not not_179 (not_179_out, AdSub);
  not not_180 (not_180_out, A1);
  not not_181 (not_181_out, B0);
  not not_182 (not_182_out, B2);
  not not_183 (not_183_out, B3);
  not not_184 (not_184_out, AdSub);
  not not_185 (not_185_out, A2);
  not not_186 (not_186_out, B0);
  not not_187 (not_187_out, B1);
  not not_188 (not_188_out, B3);
  not not_189 (not_189_out, AdSub);
  not not_190 (not_190_out, A2);
  not not_191 (not_191_out, B2);
  not not_192 (not_192_out, B3);
  not not_193 (not_193_out, AdSub);
  not not_194 (not_194_out, B0);
  not not_195 (not_195_out, B1);
  not not_196 (not_196_out, B2);
  not not_197 (not_197_out, B3);
  not not_198 (not_198_out, A2);
  not not_199 (not_199_out, A1);
  not not_200 (not_200_out, A2);
  not not_201 (not_201_out, A0);
  not not_202 (not_202_out, A1);
  not not_203 (not_203_out, A2);
  not not_204 (not_204_out, A0);
  not not_205 (not_205_out, A1);
  not not_206 (not_206_out, A0);
  not not_207 (not_207_out, A2);
  not not_208 (not_208_out, A3);
  not not_209 (not_209_out, B0);
  not not_210 (not_210_out, B1);
  not not_211 (not_211_out, A3);
  not not_212 (not_212_out, B2);
  not not_213 (not_213_out, A3);
  not not_214 (not_214_out, B3);
  not not_215 (not_215_out, AdSub);
  not not_216 (not_216_out, B0);
  not not_217 (not_217_out, B1);
  not not_218 (not_218_out, B3);
  not not_219 (not_219_out, B2);
  not not_220 (not_220_out, B3);
  not not_221 (not_221_out, AdSub);
  not not_222 (not_222_out, A1);
  not not_223 (not_223_out, A0);
  not not_224 (not_224_out, A3);
  not not_225 (not_225_out, B1);
  not not_226 (not_226_out, B2);
  not not_227 (not_227_out, A2);
  not not_228 (not_228_out, A3);
  not not_229 (not_229_out, B0);
  not not_230 (not_230_out, B2);
  not not_231 (not_231_out, A2);
  not not_232 (not_232_out, A3);
  not not_233 (not_233_out, B3);
  not not_234 (not_234_out, A0);
  not not_235 (not_235_out, A3);
  not not_236 (not_236_out, B3);
  not not_237 (not_237_out, A0);
  not not_238 (not_238_out, B1);
  not not_239 (not_239_out, B2);
  not not_240 (not_240_out, B3);
  not not_241 (not_241_out, A2);
  not not_242 (not_242_out, B0);
  not not_243 (not_243_out, B2);
  not not_244 (not_244_out, B3);
  not not_245 (not_245_out, A2);
  not not_246 (not_246_out, A0);
  not not_247 (not_247_out, A3);
  not not_248 (not_248_out, B0);
  not not_249 (not_249_out, A3);
  not not_250 (not_250_out, B1);
  not not_251 (not_251_out, A3);
  not not_252 (not_252_out, B3);
  not not_253 (not_253_out, AdSub);
  not not_254 (not_254_out, B0);
  not not_255 (not_255_out, B3);
  not not_256 (not_256_out, B1);
  not not_257 (not_257_out, B3);
  not not_258 (not_258_out, AdSub);
  not not_259 (not_259_out, A1);
  not not_260 (not_260_out, A3);
  not not_261 (not_261_out, B1);
  not not_262 (not_262_out, B2);
  not not_263 (not_263_out, A1);
  not not_264 (not_264_out, A3);
  not not_265 (not_265_out, B3);
  not not_266 (not_266_out, A1);
  not not_267 (not_267_out, B1);
  not not_268 (not_268_out, B2);
  not not_269 (not_269_out, B3);
  not not_270 (not_270_out, A1);
  not not_271 (not_271_out, A3);
  not not_272 (not_272_out, B1);
  not not_273 (not_273_out, A3);
  not not_274 (not_274_out, B3);
  not not_275 (not_275_out, AdSub);
  not not_276 (not_276_out, B1);
  not not_277 (not_277_out, B3);
  not not_278 (not_278_out, AdSub);
  not not_279 (not_279_out, A2);
  not not_280 (not_280_out, A3);
  not not_281 (not_281_out, B2);
  not not_282 (not_282_out, A2);
  not not_283 (not_283_out, A3);
  not not_284 (not_284_out, B3);
  not not_285 (not_285_out, A2);
  not not_286 (not_286_out, B2);
  not not_287 (not_287_out, B3);
  not not_288 (not_288_out, A2);
  not not_289 (not_289_out, A3);
  not not_290 (not_290_out, A3);
  not not_291 (not_291_out, B3);
  not not_292 (not_292_out, AdSub);
  not not_293 (not_293_out, B3);
  not not_294 (not_294_out, AdSub);
  not not_295 (not_295_out, A3);
  not not_296 (not_296_out, A2);
  not not_297 (not_297_out, A3);
  not not_298 (not_298_out, A2);
  not not_299 (not_299_out, A1);
  not not_300 (not_300_out, A2);
  not not_301 (not_301_out, A3);
  not not_302 (not_302_out, A1);
  not not_303 (not_303_out, A3);
  not not_304 (not_304_out, A0);
  not not_305 (not_305_out, A1);
  not not_306 (not_306_out, A2);
  not not_307 (not_307_out, A3);
  not not_308 (not_308_out, A0);
  not not_309 (not_309_out, A1);
  not not_310 (not_310_out, A2);
  not not_311 (not_311_out, A0);
  not not_312 (not_312_out, A1);
  not not_313 (not_313_out, A3);
  not not_314 (not_314_out, A0);
  not not_315 (not_315_out, A1);
  not not_316 (not_316_out, A0);
  not not_317 (not_317_out, A2);
  not not_318 (not_318_out, A3);
  not not_319 (not_319_out, A0);
  not not_320 (not_320_out, A3);
  not not_321 (not_321_out, AdSub);
  not not_322 (not_322_out, A1);
  not not_323 (not_323_out, A2);
  not not_324 (not_324_out, A1);
  not not_325 (not_325_out, A0);
  not not_326 (not_326_out, A2);
  not not_327 (not_327_out, A0);
  not not_328 (not_328_out, A3);
  not not_329 (not_329_out, AdSub);
  not not_330 (not_330_out, A2);
  not not_331 (not_331_out, AdSub);
  not not_332 (not_332_out, A3);
  not not_333 (not_333_out, AdSub);
  not not_334 (not_334_out, A2);
  not not_335 (not_335_out, AdSub);
  not not_336 (not_336_out, A3);
  not not_337 (not_337_out, AdSub);
  not not_338 (not_338_out, A2);
  not not_339 (not_339_out, AdSub);
  not not_340 (not_340_out, A3);
  not not_341 (not_341_out, AdSub);
  and and_1 (and_1_out, not_1_out, B0);
  and and_2 (and_2_out, A0, not_2_out);
  and and_3 (and_3_out, not_3_out, not_4_out, B1, not_5_out);
  and and_4 (and_4_out, not_6_out, not_7_out, B1);
  and and_5 (and_5_out, not_8_out, not_9_out, B0, not_10_out, AdSub);
  and and_6 (and_6_out, not_11_out, A1, not_12_out, not_13_out);
  and and_7 (and_7_out, A1, not_14_out, not_15_out);
  and and_8 (and_8_out, not_16_out, A1, B0, B1, AdSub);
  and and_9 (and_9_out, A0, not_17_out, B1, AdSub);
  and and_10 (and_10_out, A0, not_18_out, B0, not_19_out, not_20_out);
  and and_11 (and_11_out, A0, A1, not_21_out, AdSub);
  and and_12 (and_12_out, A0, A1, B0, B1, not_22_out);
  and and_13 (and_13_out, not_23_out, not_24_out, not_25_out, B2, not_26_out);
  and and_14 (and_14_out, not_27_out, not_28_out, not_29_out, B2, not_30_out);
  and and_15 (and_15_out, not_31_out, not_32_out, not_33_out, B2);
  and and_16 (and_16_out, not_34_out, not_35_out, B1, not_36_out, AdSub);
  and and_17 (and_17_out, not_37_out, not_38_out, not_39_out, B0, not_40_out, AdSub);
  and and_18 (and_18_out, not_41_out, not_42_out, A2, not_43_out, not_44_out);
  and and_19 (and_19_out, not_45_out, A2, not_46_out, not_47_out, not_48_out);
  and and_20 (and_20_out, A2, not_49_out, not_50_out, not_51_out);
  and and_21 (and_21_out, not_52_out, A2, B1, B2, AdSub);
  and and_22 (and_22_out, not_53_out, not_54_out, A2, B0, B2, AdSub);
  and and_23 (and_23_out, not_55_out, A1, not_56_out, not_57_out, B2);
  and and_24 (and_24_out, A1, not_58_out, not_59_out, B2, AdSub);
  and and_25 (and_25_out, A1, not_60_out, B1, not_61_out, not_62_out);
  and and_26 (and_26_out, not_63_out, A1, not_64_out, B0, B1, not_65_out);
  and and_27 (and_27_out, not_66_out, A1, A2, not_67_out, not_68_out);
  and and_28 (and_28_out, A1, A2, not_69_out, not_70_out, AdSub);
  and and_29 (and_29_out, A1, A2, B1, B2, not_71_out);
  and and_30 (and_30_out, not_72_out, A1, A2, B0, B1, B2);
  and and_31 (and_31_out, A0, not_73_out, not_74_out, not_75_out, B2);
  and and_32 (and_32_out, A0, not_76_out, B0, B1, not_77_out, not_78_out);
  and and_33 (and_33_out, A0, not_79_out, A2, not_80_out, not_81_out);
  and and_34 (and_34_out, A0, A2, B0, B1, B2, not_82_out);
  and and_35 (and_35_out, A0, A1, not_83_out, B2, AdSub);
  and and_36 (and_36_out, A0, A1, not_84_out, B0, not_85_out, not_86_out);
  and and_37 (and_37_out, A0, A1, A2, not_87_out, AdSub);
  and and_38 (and_38_out, A0, A1, A2, B0, B2, not_88_out);
  and and_39 (and_39_out, not_89_out, not_90_out, not_91_out, not_92_out, B3, not_93_out);
  and and_40 (and_40_out, not_94_out, not_95_out, not_96_out, not_97_out, B3, not_98_out);
  and and_41 (and_41_out, not_99_out, not_100_out, not_101_out, not_102_out, B3, not_103_out);
  and and_42 (and_42_out, not_104_out, not_105_out, not_106_out, not_107_out, B3, not_108_out);
  and and_43 (and_43_out, not_109_out, not_110_out, not_111_out, not_112_out, B3, not_113_out);
  and and_44 (and_44_out, not_114_out, not_115_out, not_116_out, not_117_out, B3, not_118_out);
  and and_45 (and_45_out, not_119_out, not_120_out, not_121_out, not_122_out, B3, not_123_out);
  and and_46 (and_46_out, not_124_out, not_125_out, not_126_out, B3, not_127_out);
  and and_47 (and_47_out, not_128_out, not_129_out, not_130_out, not_131_out, B3);
  and and_48 (and_48_out, not_132_out, not_133_out, B2, not_134_out, AdSub);
  and and_49 (and_49_out, not_135_out, not_136_out, not_137_out, B1, not_138_out, AdSub);
  and and_50 (and_50_out, not_139_out, not_140_out, B1, B2, not_141_out, AdSub);
  and and_51 (and_51_out, not_142_out, not_143_out, not_144_out, not_145_out, B0, not_146_out, AdSub);
  and and_52 (and_52_out, not_147_out, not_148_out, not_149_out, B0, B2, not_150_out, AdSub);
  and and_53 (and_53_out, not_151_out, not_152_out, not_153_out, B0, B1, not_154_out, AdSub);
  and and_54 (and_54_out, not_155_out, not_156_out, not_157_out, A3, not_158_out, not_159_out);
  and and_55 (and_55_out, not_160_out, not_161_out, A3, not_162_out, not_163_out, not_164_out);
  and and_56 (and_56_out, not_165_out, not_166_out, A3, not_167_out, not_168_out, not_169_out);
  and and_57 (and_57_out, not_170_out, not_171_out, A3, not_172_out, not_173_out, not_174_out);
  and and_58 (and_58_out, not_175_out, not_176_out, A3, not_177_out, not_178_out, not_179_out);
  and and_59 (and_59_out, not_180_out, A3, not_181_out, not_182_out, not_183_out, not_184_out);
  and and_60 (and_60_out, not_185_out, A3, not_186_out, not_187_out, not_188_out, not_189_out);
  and and_61 (and_61_out, not_190_out, A3, not_191_out, not_192_out, not_193_out);
  and and_62 (and_62_out, A3, not_194_out, not_195_out, not_196_out, not_197_out);
  and and_63 (and_63_out, not_198_out, A3, B2, B3, AdSub);
  and and_64 (and_64_out, not_199_out, not_200_out, A3, B1, B3, AdSub);
  and and_65 (and_65_out, not_201_out, not_202_out, not_203_out, A3, B0, B3, AdSub);
  and and_66 (and_66_out, not_204_out, not_205_out, A3, B0, B2, B3, AdSub);
  and and_67 (and_67_out, not_206_out, not_207_out, A3, B0, B1, B3, AdSub);
  and and_68 (and_68_out, A2, not_208_out, not_209_out, not_210_out, B3, AdSub);
  and and_69 (and_69_out, A2, not_211_out, not_212_out, B3, AdSub);
  and and_70 (and_70_out, A2, not_213_out, B2, not_214_out, not_215_out);
  and and_71 (and_71_out, A2, A3, not_216_out, not_217_out, not_218_out, AdSub);
  and and_72 (and_72_out, A2, A3, not_219_out, not_220_out, AdSub);
  and and_73 (and_73_out, A2, A3, B2, B3, not_221_out);
  and and_74 (and_74_out, not_222_out, A2, A3, B1, B2, B3);
  and and_75 (and_75_out, not_223_out, A1, not_224_out, not_225_out, not_226_out, B3);
  and and_76 (and_76_out, A1, not_227_out, not_228_out, not_229_out, not_230_out, B3);
  and and_77 (and_77_out, A1, not_231_out, not_232_out, B1, B2, not_233_out);
  and and_78 (and_78_out, not_234_out, A1, not_235_out, B0, B1, B2, not_236_out);
  and and_79 (and_79_out, not_237_out, A1, A3, not_238_out, not_239_out, not_240_out);
  and and_80 (and_80_out, A1, not_241_out, A3, not_242_out, not_243_out, not_244_out);
  and and_81 (and_81_out, A1, not_245_out, A3, B1, B2, B3);
  and and_82 (and_82_out, not_246_out, A1, A3, B0, B1, B2, B3);
  and and_83 (and_83_out, A1, A2, not_247_out, not_248_out, B3, AdSub);
  and and_84 (and_84_out, A1, A2, not_249_out, not_250_out, B3, AdSub);
  and and_85 (and_85_out, A1, A2, not_251_out, B1, not_252_out, not_253_out);
  and and_86 (and_86_out, A1, A2, A3, not_254_out, not_255_out, AdSub);
  and and_87 (and_87_out, A1, A2, A3, not_256_out, not_257_out, AdSub);
  and and_88 (and_88_out, A1, A2, A3, B1, B3, not_258_out);
  and and_89 (and_89_out, A0, not_259_out, not_260_out, not_261_out, not_262_out, B3);
  and and_90 (and_90_out, A0, not_263_out, not_264_out, B0, B1, B2, not_265_out);
  and and_91 (and_91_out, A0, not_266_out, A3, not_267_out, not_268_out, not_269_out);
  and and_92 (and_92_out, A0, not_270_out, A3, B0, B1, B2, B3);
  and and_93 (and_93_out, A0, A2, not_271_out, not_272_out, B3, AdSub);
  and and_94 (and_94_out, A0, A2, not_273_out, B0, B1, not_274_out, not_275_out);
  and and_95 (and_95_out, A0, A2, A3, not_276_out, not_277_out, AdSub);
  and and_96 (and_96_out, A0, A2, A3, B0, B1, B3, not_278_out);
  and and_97 (and_97_out, A0, A1, not_279_out, not_280_out, not_281_out, B3);
  and and_98 (and_98_out, A0, A1, not_282_out, not_283_out, B0, B2, not_284_out);
  and and_99 (and_99_out, A0, A1, not_285_out, A3, not_286_out, not_287_out);
  and and_100 (and_100_out, A0, A1, not_288_out, A3, B0, B2, B3);
  and and_101 (and_101_out, A0, A1, A2, not_289_out, B3, AdSub);
  and and_102 (and_102_out, A0, A1, A2, not_290_out, B0, not_291_out, not_292_out);
  and and_103 (and_103_out, A0, A1, A2, A3, not_293_out, AdSub);
  and and_104 (and_104_out, A0, A1, A2, A3, B0, B3, not_294_out);
  and and_105 (and_105_out, not_295_out, B3, AdSub);
  and and_106 (and_106_out, not_296_out, not_297_out, B2, AdSub);
  and and_107 (and_107_out, not_298_out, B2, B3, AdSub);
  and and_108 (and_108_out, not_299_out, not_300_out, not_301_out, B1, AdSub);
  and and_109 (and_109_out, not_302_out, not_303_out, B1, B2, AdSub);
  and and_110 (and_110_out, not_304_out, not_305_out, not_306_out, not_307_out, B0, AdSub);
  and and_111 (and_111_out, not_308_out, not_309_out, not_310_out, B0, B3, AdSub);
  and and_112 (and_112_out, not_311_out, not_312_out, not_313_out, B0, B2, AdSub);
  and and_113 (and_113_out, not_314_out, not_315_out, B0, B2, B3, AdSub);
  and and_114 (and_114_out, not_316_out, not_317_out, not_318_out, B0, B1, AdSub);
  and and_115 (and_115_out, not_319_out, not_320_out, B0, B1, B2, AdSub);
  and and_116 (and_116_out, A3, B3, not_321_out);
  and and_117 (and_117_out, not_322_out, not_323_out, A3, B1, B3);
  and and_118 (and_118_out, not_324_out, A3, B1, B2, B3);
  and and_119 (and_119_out, not_325_out, not_326_out, A3, B0, B1, B3);
  and and_120 (and_120_out, not_327_out, A3, B0, B1, B2, B3);
  and and_121 (and_121_out, A2, not_328_out, B2, B3);
  and and_122 (and_122_out, A2, A3, B2, not_329_out);
  and and_123 (and_123_out, A1, not_330_out, B1, B2, B3);
  and and_124 (and_124_out, A1, A3, B1, B2, not_331_out);
  and and_125 (and_125_out, A1, A2, not_332_out, B1, B3);
  and and_126 (and_126_out, A1, A2, A3, B1, not_333_out);
  and and_127 (and_127_out, A0, not_334_out, B0, B1, B2, B3);
  and and_128 (and_128_out, A0, A3, B0, B1, B2, not_335_out);
  and and_129 (and_129_out, A0, A2, not_336_out, B0, B1, B3);
  and and_130 (and_130_out, A0, A2, A3, B0, B1, not_337_out);
  and and_131 (and_131_out, A0, A1, not_338_out, B0, B2, B3);
  and and_132 (and_132_out, A0, A1, A3, B0, B2, not_339_out);
  and and_133 (and_133_out, A0, A1, A2, not_340_out, B0, B3);
  and and_134 (and_134_out, A0, A1, A2, A3, B0, not_341_out);
  or or_1 (S0, and_1_out, and_2_out);
  or or_2 (S1, and_3_out, and_4_out, and_5_out, and_6_out, and_7_out, and_8_out, and_9_out, and_10_out, and_11_out, and_12_out);
  or or_3 (S2, and_13_out, and_14_out, and_15_out, and_16_out, and_17_out, and_18_out, and_19_out, and_20_out, and_21_out, and_22_out, and_23_out, and_24_out, and_25_out, and_26_out, and_27_out, and_28_out, and_29_out, and_30_out, and_31_out, and_32_out, and_33_out, and_34_out, and_35_out, and_36_out, and_37_out, and_38_out);
  or or_4 (or_4_out, and_39_out, and_40_out, and_41_out, and_42_out, and_43_out, and_44_out, and_45_out, and_46_out, and_47_out, and_48_out, and_49_out, and_50_out, and_51_out, and_52_out, and_53_out, and_54_out, and_55_out, and_56_out, and_57_out, and_58_out, and_59_out, and_60_out);
  or or_5 (or_5_out, and_61_out, and_62_out, and_63_out, and_64_out, and_65_out, and_66_out, and_67_out, and_68_out, and_69_out, and_70_out, and_71_out, and_72_out, and_73_out, and_74_out, and_75_out, and_76_out, and_77_out, and_78_out, and_79_out, and_80_out, and_81_out, and_82_out);
  or or_6 (or_6_out, and_83_out, and_84_out, and_85_out, and_86_out, and_87_out, and_88_out, and_89_out, and_90_out, and_91_out, and_92_out, and_93_out, and_94_out, and_95_out, and_96_out, and_97_out, and_98_out, and_99_out, and_100_out, and_101_out, and_102_out, and_103_out, and_104_out);
  or or_7 (S3, or_4_out, or_5_out, or_6_out);
  or or_8 (Overflow, and_105_out, and_106_out, and_107_out, and_108_out, and_109_out, and_110_out, and_111_out, and_112_out, and_113_out, and_114_out, and_115_out, and_116_out, and_117_out, and_118_out, and_119_out, and_120_out, and_121_out, and_122_out, and_123_out, and_124_out, and_125_out, and_126_out, and_127_out, and_128_out, and_129_out, and_130_out, and_131_out, and_132_out, and_133_out, and_134_out);
endmodule

module Display (
  input  a,
  input  b,
  input  c,
  input  d,
  input  e,
  output a2,
  output b2,
  output c2,
  output d2,
  output e2,
  output f,
  output g,
  output h
);

  wire and_1_out, and_2_out, and_3_out, and_4_out, and_5_out, and_6_out, and_7_out, and_8_out, and_9_out,
       and_10_out, and_11_out, and_12_out, and_13_out, and_14_out, and_15_out, and_16_out, and_17_out,
       and_18_out, and_19_out, and_20_out, and_21_out, and_22_out, and_23_out, and_24_out, and_25_out,
       and_26_out, and_27_out, and_28_out, and_29_out, and_30_out, not_1_out, not_2_out, not_3_out,
       not_4_out, not_5_out, not_6_out, not_7_out, not_8_out, not_9_out, not_10_out, not_11_out, not_12_out,
       not_13_out, not_14_out, not_15_out, not_16_out, not_17_out, not_18_out, not_19_out, not_20_out,
       not_21_out, not_22_out, not_23_out, not_24_out, not_25_out, not_26_out, not_27_out, not_28_out,
       not_29_out, not_30_out, not_31_out, not_32_out, not_33_out, not_34_out, not_35_out, not_36_out,
       not_37_out, not_38_out, not_39_out, not_40_out, not_41_out, not_42_out, not_43_out, not_44_out,
       not_45_out, not_46_out, not_47_out, not_48_out, not_49_out, not_50_out, not_51_out, not_52_out,
       not_53_out, not_54_out, not_55_out, not_56_out, not_57_out, not_58_out, not_59_out, not_60_out,
       not_61_out, not_62_out, not_63_out, not_64_out, not_65_out, not_66_out, not_67_out, not_68_out,
       not_69_out, not_70_out, not_71_out, not_72_out, not_73_out, not_74_out, not_75_out, not_76_out,
       not_77_out, not_78_out, not_79_out, not_80_out, not_81_out, not_82_out, not_83_out, not_84_out,
       not_85_out, not_86_out, not_87_out, not_88_out, not_89_out, not_90_out;

  not not_1 (not_1_out, b);
  not not_2 (not_2_out, c);
  not not_3 (not_3_out, d);
  not not_4 (not_4_out, e);
  not not_5 (not_5_out, a);
  not not_6 (not_6_out, e);
  not not_7 (not_7_out, a);
  not not_8 (not_8_out, e);
  not not_9 (not_9_out, b);
  not not_10 (not_10_out, c);
  not not_11 (not_11_out, d);
  not not_12 (not_12_out, b);
  not not_13 (not_13_out, c);
  not not_14 (not_14_out, e);
  not not_15 (not_15_out, a);
  not not_16 (not_16_out, b);
  not not_17 (not_17_out, e);
  not not_18 (not_18_out, a);
  not not_19 (not_19_out, c);
  not not_20 (not_20_out, d);
  not not_21 (not_21_out, e);
  not not_22 (not_22_out, b);
  not not_23 (not_23_out, c);
  not not_24 (not_24_out, e);
  not not_25 (not_25_out, a);
  not not_26 (not_26_out, e);
  not not_27 (not_27_out, b);
  not not_28 (not_28_out, c);
  not not_29 (not_29_out, d);
  not not_30 (not_30_out, b);
  not not_31 (not_31_out, c);
  not not_32 (not_32_out, e);
  not not_33 (not_33_out, a);
  not not_34 (not_34_out, e);
  not not_35 (not_35_out, a);
  not not_36 (not_36_out, e);
  not not_37 (not_37_out, b);
  not not_38 (not_38_out, c);
  not not_39 (not_39_out, d);
  not not_40 (not_40_out, b);
  not not_41 (not_41_out, c);
  not not_42 (not_42_out, d);
  not not_43 (not_43_out, e);
  not not_44 (not_44_out, a);
  not not_45 (not_45_out, b);
  not not_46 (not_46_out, e);
  not not_47 (not_47_out, a);
  not not_48 (not_48_out, d);
  not not_49 (not_49_out, e);
  not not_50 (not_50_out, a);
  not not_51 (not_51_out, c);
  not not_52 (not_52_out, e);
  not not_53 (not_53_out, b);
  not not_54 (not_54_out, c);
  not not_55 (not_55_out, d);
  not not_56 (not_56_out, e);
  not not_57 (not_57_out, a);
  not not_58 (not_58_out, d);
  not not_59 (not_59_out, e);
  not not_60 (not_60_out, b);
  not not_61 (not_61_out, c);
  not not_62 (not_62_out, d);
  not not_63 (not_63_out, e);
  not not_64 (not_64_out, a);
  not not_65 (not_65_out, c);
  not not_66 (not_66_out, e);
  not not_67 (not_67_out, a);
  not not_68 (not_68_out, d);
  not not_69 (not_69_out, e);
  not not_70 (not_70_out, b);
  not not_71 (not_71_out, c);
  not not_72 (not_72_out, d);
  not not_73 (not_73_out, b);
  not not_74 (not_74_out, c);
  not not_75 (not_75_out, e);
  not not_76 (not_76_out, a);
  not not_77 (not_77_out, b);
  not not_78 (not_78_out, e);
  not not_79 (not_79_out, a);
  not not_80 (not_80_out, c);
  not not_81 (not_81_out, e);
  not not_82 (not_82_out, a);
  not not_83 (not_83_out, d);
  not not_84 (not_84_out, e);
  not not_85 (not_85_out, b);
  not not_86 (not_86_out, c);
  not not_87 (not_87_out, d);
  not not_88 (not_88_out, b);
  not not_89 (not_89_out, c);
  not not_90 (not_90_out, e);
  and and_1 (and_1_out, not_1_out, not_2_out, not_3_out, not_4_out);
  and and_2 (and_2_out, not_5_out, c, not_6_out);
  and and_3 (and_3_out, not_7_out, b, d, not_8_out);
  and and_4 (and_4_out, a, not_9_out, not_10_out, not_11_out);
  and and_5 (and_5_out, a, not_12_out, not_13_out, not_14_out);
  and and_6 (and_6_out, not_15_out, not_16_out, not_17_out);
  and and_7 (and_7_out, not_18_out, not_19_out, not_20_out, not_21_out);
  and and_8 (and_8_out, not_22_out, not_23_out, not_24_out);
  and and_9 (and_9_out, not_25_out, c, d, not_26_out);
  and and_10 (and_10_out, a, not_27_out, not_28_out, not_29_out);
  and and_11 (and_11_out, not_30_out, not_31_out, not_32_out);
  and and_12 (and_12_out, not_33_out, d, not_34_out);
  and and_13 (and_13_out, not_35_out, b, not_36_out);
  and and_14 (and_14_out, a, not_37_out, not_38_out, not_39_out);
  and and_15 (and_15_out, not_40_out, not_41_out, not_42_out, not_43_out);
  and and_16 (and_16_out, not_44_out, not_45_out, c, not_46_out);
  and and_17 (and_17_out, not_47_out, c, not_48_out, not_49_out);
  and and_18 (and_18_out, not_50_out, b, not_51_out, d, not_52_out);
  and and_19 (and_19_out, not_53_out, not_54_out, not_55_out, not_56_out);
  and and_20 (and_20_out, not_57_out, c, not_58_out, not_59_out);
  and and_21 (and_21_out, not_60_out, not_61_out, not_62_out, not_63_out);
  and and_22 (and_22_out, not_64_out, b, not_65_out, not_66_out);
  and and_23 (and_23_out, not_67_out, b, not_68_out, not_69_out);
  and and_24 (and_24_out, a, not_70_out, not_71_out, not_72_out);
  and and_25 (and_25_out, a, not_73_out, not_74_out, not_75_out);
  and and_26 (and_26_out, not_76_out, not_77_out, c, not_78_out);
  and and_27 (and_27_out, not_79_out, b, not_80_out, not_81_out);
  and and_28 (and_28_out, not_82_out, b, not_83_out, not_84_out);
  and and_29 (and_29_out, a, not_85_out, not_86_out, not_87_out);
  and and_30 (and_30_out, a, not_88_out, not_89_out, not_90_out);
  or or_1 (a2, and_1_out, and_2_out, and_3_out, and_4_out, and_5_out);
  or or_2 (b2, and_6_out, and_7_out, and_8_out, and_9_out, and_10_out);
  or or_3 (c2, and_11_out, and_12_out, and_13_out, and_14_out);
  or or_4 (d2, and_15_out, and_16_out, and_17_out, and_18_out);
  or or_5 (e2, and_19_out, and_20_out);
  or or_6 (f, and_21_out, and_22_out, and_23_out, and_24_out, and_25_out);
  or or_7 (g, and_26_out, and_27_out, and_28_out, and_29_out, and_30_out);

  assign h = e;
endmodule

module teste (
);

  somador somador_1 ();  // open: A3, A2, A1, A0, B3, B2, B1, B0, S0, S1, S2, S3, S4
endmodule
